# Fritzing sketch Sketch (saved by Fritzing 0.8.5b)
breadboards: 1

parts:
  Part1 = Arduino Uno (Rev3)
  S1 = Pushbutton [package="[THT]"]
  R1 = Resistor [tolerance=±5% resistance=10k package=THT]
  LED1 = LED - 5mm [color="Red (633nm)" package="5 mm [THT]"]
  R2 = Resistor [tolerance=±5% resistance=220 package=THT]
  SPKR1 = Loudspeaker
  R3 = Resistor [tolerance=±5% resistance=220 package=THT]

nets:
  N1: Part1.D10_PWM/SS, SPKR1.pin1
  N2: Part1.D13/SCK, R2.Pin_0
  N3: Part1.GND, R1.Pin_1, LED1.anode, R3.Pin_0
  N4: Part1.D3_PWM, S1.Pin_1, S1.Pin_2, R1.Pin_0
  N5: Part1.5V, S1.Pin_3, S1.Pin_4
  N6: LED1.cathode, R2.Pin_1
  N7: SPKR1.pin2, R3.Pin_1
